// Logisim project hrmcpu.circ as structural Verilog: 9 circuits, main circuit top
module top (
  input  rst
);

  wire alu_1_flag, branch, ControlUnit_p1, empty, fb, full, ijump, muxM, rIN, rstPC, srcA, wIR, wM, wO, wPC,
       wR;
  wire [1:0] muxR;
  wire [2:0] aluCtl;
  wire [7:0] alu_1_aluout, inbox_1_din, INSTR, memory_1_m, pc_1_pc, r_1_r;

  // Probe on inbox_1_din
  INBOX inbox_1 (.rIn(rIN), .rst(rst), .empty(empty), .DIN(inbox_1_din));
  // Probe on r_1_r
  R r_1 (.iInbox(inbox_1_din), .iMem(memory_1_m), .iAlu(alu_1_aluout), .muxR(muxR), .wR(wR), .R(r_1_r));
  // Probe on memory_1_m
  MEMORY memory_1 (
    .PC(pc_1_pc), .srcA(srcA), .wM(wM), .R(r_1_r), .aluOut(alu_1_aluout), .muxM(muxM), .fb(fb), .M(memory_1_m));
  // Probe on INSTR
  IR ir_1 (.nIR(memory_1_m), .wIR(wIR), .rIR(INSTR));
  PC pc_1 (
    .branch(branch), .ijump(ijump), .aluFlag(alu_1_flag), .jmpAddr(memory_1_m), .wPC(wPC), .rst(rstPC),
    .PC(pc_1_pc));
  // Probe on pc_1_pc
  ALU alu_1 (.inR(r_1_r), .inM(memory_1_m), .aluCtl(aluCtl), .flag(alu_1_flag), .aluOut(alu_1_aluout));
  // FSM_Entity #(.content("fsm ControlUnit @[ 34 , 30 , 1200 , 700 ]\n{ in INSTR [ 8 ] @[ 34 , 100 , 71 , 15 ]\n;\nin inEmpty [ 1 ] @[ 34 , 140 , 55 , 15 ]\n;\nin outFull [ 1 ] @[ 34 , 178 , 48 , 15 ]\n;\nout wIR [ 1 ] @[ 1208 , 93 , 26 , 15 ]\n;\nout muxR [ 2 ] @[ 1165 , 150 , 69 , 15 ]\n;\nout wR [ 1 ] @[ 1211 , 177 , 23 , 15 ]\n;\nout muxM [ 1 ] @[ 1193 , 222 , 41 , 15 ]\n;\nout srcA [ 1 ] @[ 1201 , 244 , 33 , 15 ]\n;\nout wM [ 1 ] @[ 1209 , 268 , 25 , 15 ]\n;\nout fb [ 1 ] @[ 1216 , 303 , 18 , 15 ]\n;\nout aluCtl [ 3 ] @[ 1163 , 333 , 71 , 15 ]\n;\nout wPC [ 1 ] @[ 1203 , 366 , 31 , 15 ]\n;\nout rIn [ 1 ] @[ 1212 , 390 , 22 , 15 ]\n;\nout wO [ 1 ] @[ 1210 , 415 , 24 , 15 ]\n;\nout ijump [ 1 ] @[ 1195 , 467 , 39 , 15 ]\n;\nout branch [ 1 ] @[ 1184 , 490 , 50 , 15 ]\n;\nout rst [ 1 ] @[ 1211 , 523 , 23 , 15 ]\n;\ncodeWidth = 4 ; reset = RESET ; state RESET = \"0000\" @[ 164 , 91 , 30 , 30 ]\n{\ncommands @[ 209 , 106 , 53 , 21 ]\n{\nrst = \"1\" ;\n}\ntransitions {\nRESET -> FETCH1 when default @[ 293 , 74 , 50 , 21 ]\n;\n}\n}\nstate INCRPC = \"0010\" @[ 172 , 171 , 30 , 30 ]\n{\ncommands @[ 217 , 186 , 61 , 21 ]\n{\nwPC = \"1\" ;\n}\ntransitions {\nINCRPC -> FETCH1 when default @[ 255 , 144 , 50 , 21 ]\n;\n}\n}\nstate FETCH1 = \"0100\" @[ 342 , 119 , 30 , 30 ]\n{\ncommands @[ 387 , 134 , 63 , 21 ]\n{\nsrcA = \"1\" ;\n}\ntransitions {\nFETCH1 -> FETCH2 when default @[ 269 , 210 , 50 , 21 ]\n;\n}\n}\nstate FETCH2 = \"0110\" @[ 306 , 282 , 30 , 30 ]\n{\ncommands @[ 351 , 297 , 61 , 36 ]\n{\nwIR = \"1\" ;\nwPC = \"1\" ;\n}\ntransitions {\nFETCH2 -> FETCH1 when default @[ 314 , 237 , 50 , 21 ]\n;\nFETCH2 -> INBOX1 when INSTR [ 7 : 4 ] == \"0000\" @[ 144 , 403 , 143 , 21 ]\n;\nFETCH2 -> OUTBOX when INSTR [ 7 : 4 ] == \"0001\" @[ 229 , 379 , 143 , 21 ]\n;\n}\n}\nstate INBOX1 = \"1000\" @[ 166 , 430 , 30 , 30 ]\n{\ncommands @[ 212 , 445 , 52 , 21 ]\n{\nrIn = \"1\" ;\n}\ntransitions {\nINBOX1 -> INBOX2 when default @[ 153 , 495 , 50 , 21 ]\n;\n}\n}\nstate INBOX2 = \"1010\" @[ 159 , 527 , 30 , 30 ]\n{\ncommands @[ 205 , 542 , 77 , 36 ]\n{\nmuxR = \"00\" ;\nwR = \"1\" ;\n}\ntransitions {\nINBOX2 -> FETCH1 when default @[ 335 , 515 , 50 , 21 ]\n;\n}\n}\nstate OUTBOX = \"0001\" @[ 297 , 436 , 30 , 30 ]\n{\ncommands @[ 343 , 451 , 54 , 21 ]\n{\nwO = \"1\" ;\n}\ntransitions {\nOUTBOX -> FETCH1 when default @[ 399 , 377 , 50 , 21 ]\n;\n}\n}\n}")) ControlUnit: pin names not known; wires that end beside it: ControlUnit_p1, rst, 1'b1, INSTR, empty, full, wIR, muxR, wR, muxM, srcA, wM, fb, aluCtl, wPC, rIN, wO, ijump
  Clock clock_1 (.out(ControlUnit_p1));
  OUTBOX outbox_1 (.DOUT(r_1_r), .wO(wO), .full(full));
endmodule

module PC (
  input  branch,
  input  ijump,
  input  aluFlag,
  input  [7:0] jmpAddr,
  input  wPC,
  input  rst,
  output [7:0] PC
);

  wire and_1_out, clock_1_out, or_1_out, or_2_out;
  wire [7:0] adder_1_out, multiplexer_1_out, multiplexer_2_out;

  or or_1 (or_1_out, ijump, aluFlag);
  and and_1 (and_1_out, branch, or_1_out);
  Multiplexer #(.width(8), .enable("false")) multiplexer_1 (
    .in0(adder_1_out), .in1(jmpAddr), .out(multiplexer_1_out), .sel(and_1_out));
  Multiplexer #(.width(8), .enable("false")) multiplexer_2 (
    .in0(multiplexer_1_out), .in1(8'h20), .out(multiplexer_2_out), .sel(rst));
  // Probe on multiplexer_2_out
  or or_2 (or_2_out, rst, wPC);
  Register rPC (.D(multiplexer_2_out), .en(or_2_out), .clk(clock_1_out), .Q(PC));  // open: clr
  Clock clock_1 (.out(clock_1_out));
  // Probe on adder_1_out
  Adder adder_1 (.a(PC), .b(8'h1), .out(adder_1_out));  // open: cin, cout
endmodule

module INBOX (
  input  rIn,
  input  rst,
  output empty,
  output [7:0] DIN
);

  wire clock_1_out, clock_2_out;
  wire [7:0] adder_1_out, inCursor_q, undriven;

  Clock clock_1 (.out(clock_1_out));
  Register inCursor (.D(adder_1_out), .en(rIn), .clk(clock_1_out), .Q(inCursor_q), .clr(rst));
  ROM rom_1 (.addr(inCursor_q));  // open: data
  Adder adder_1 (.a(inCursor_q), .b(8'h1), .out(adder_1_out));  // open: cin, cout
  Register inboxData (.D(undriven), .en(1'b1), .clk(clock_2_out), .Q(DIN), .clr(rst));
  Clock clock_2 (.out(clock_2_out));

  assign empty = 1'b0;

  // Notes on the sheet:
  //   contents of rom_1 (hex, n*v repeats v):
  //   1f aa bb a b
endmodule

module IR (
  input  [7:0] nIR,
  input  wIR,
  output [7:0] rIR
);

  wire clock_1_out;

  Register register_1 (.D(nIR), .en(wIR), .clk(clock_1_out), .Q(rIR));  // open: clr
  Clock clock_1 (.out(clock_1_out));
endmodule

module R (
  input  [7:0] iInbox,
  input  [7:0] iMem,
  input  [7:0] iAlu,
  input  [1:0] muxR,
  input  wR,
  output [7:0] R
);

  wire clock_1_out;
  wire [7:0] multiplexer_1_out;

  Multiplexer #(.select(2), .width(8), .enable("false")) multiplexer_1 (
    .in0(iInbox), .in1(iMem), .in3(iAlu), .out(multiplexer_1_out), .sel(muxR));  // open: in2
  Register register_1 (.D(multiplexer_1_out), .en(wR), .clk(clock_1_out), .Q(R));  // open: clr
  Clock clock_1 (.out(clock_1_out));
endmodule

module MEMORY (
  input  [7:0] PC,
  input  srcA,
  input  wM,
  input  [7:0] R,
  input  [7:0] aluOut,
  input  muxM,
  input  fb,
  output [7:0] M
);

  wire clock_1_out, clock_2_out;
  wire [7:0] indirectFeedback_q, multiplexer_1_out, multiplexer_2_out;

  Register indirectFeedback (.D(M), .en(fb), .clk(clock_1_out), .Q(indirectFeedback_q));  // open: clr
  Clock clock_1 (.out(clock_1_out));
  Multiplexer #(.width(8), .enable("false")) multiplexer_1 (
    .in0(indirectFeedback_q), .in1(PC), .out(multiplexer_1_out), .sel(srcA));
  Clock clock_2 (.out(clock_2_out));
  Multiplexer #(.width(8), .enable("false")) multiplexer_2 (.in0(R), .in1(aluOut), .out(multiplexer_2_out), .sel(muxM));
  // Probe on multiplexer_1_out
  // RAM #(.databus("bibus")) ram_1: pin names not known; wires that end beside it: multiplexer_1_out, wM

  // Notes on the sheet:
  //   Select Value Input
  //   contents of ram_1 (hex, n*v repeats v):
  //   20 0 1 30*0 10 0 10 0 10
endmodule

module ALU (
  input  [7:0] inR,
  input  [7:0] inM,
  input  [2:0] aluCtl,
  output flag,
  output [7:0] aluOut
);
endmodule

module OUTBOX (
  input  [7:0] DOUT,
  input  wO,
  output full
);

  wire clock_1_out, clock_2_out;
  wire [5:0] adder_1_out, register_1_q;

  Clock clock_1 (.out(clock_1_out));
  Register #(.width(6)) register_1 (.D(adder_1_out), .en(wO), .clk(clock_1_out), .Q(register_1_q));  // open: clr
  Adder #(.width(6)) adder_1 (.a(register_1_q), .b(6'b000001), .out(adder_1_out));  // open: cin, cout
  // RAM #(.addrWidth(6)) ram_1: pin names not known; wires that end beside it: register_1_q, DOUT
  Clock clock_2 (.out(clock_2_out));
  Comparator #(.width(6), .mode("unsigned")) comparator_1 (.a(register_1_q), .b({6{1'b1}}), .eq(full));  // open: gt, lt

  // Notes on the sheet:
  //   contents of ram_1 (hex, n*v repeats v):
  //   aa bb a
endmodule

module tmp (
  input  in_1,
  input  in_2,
  input  [1:0] muxR,
  input  in_4,
  input  in_5,
  input  in_6,
  input  in_7,
  input  in_8,
  input  ijump,
  input  [2:0] aluCtl,
  input  in_11,
  input  in_12,
  input  wPC,
  input  [2:0] in_14,
  input  wO,
  output [3:0] out_16
);

  wire clock_1_out;

  Clock clock_1 (.out(clock_1_out));
  // FSM_Entity #(.content("fsm example @[ 50 , 50 , 800 , 500 ]\n{ in A [ 3 ] @[ 50 , 100 , 44 , 15 ]\n;\nout X [ 4 ] @[ 807 , 140 , 43 , 15 ]\n;\ncodeWidth = 2 ; reset = S0 ; state S0 = \"00\" @[ 249 , 171 , 30 , 30 ]\n{\ncommands @[ 294 , 186 , 67 , 21 ]\n{\nX = \"0001\" ;\n}\ntransitions {\nS0 -> S1 when default @[ 372 , 148 , 50 , 21 ]\n;\nS0 -> S3 when A == \"000\" @[ 346 , 269 , 78 , 21 ]\n;\n}\n}\nstate S1 = \"10\" @[ 467 , 146 , 30 , 30 ]\n{\ncommands @[ 512 , 161 , 67 , 21 ]\n{\nX = \"0010\" ;\n}\ntransitions {\nS1 -> S2 when default @[ 533 , 276 , 50 , 21 ]\n;\nS1 -> S0 when A == \"000\" @[ 376 , 216 , 78 , 21 ]\n;\n}\n}\nstate S2 = \"00\" @[ 471 , 339 , 30 , 30 ]\n{\ncommands @[ 543 , 353 , 131 , 21 ]\n{\nX = { \"00\" , A [ 1 : 0 ] , \"1\" } ;\n}\ntransitions {\nS2 -> S3 when default @[ 392 , 398 , 50 , 21 ]\n;\nS2 -> S1 when A [ 2 : 1 ] == \"11\" @[ 557 , 250 , 100 , 21 ]\n;\n}\n}\nstate S3 = \"10\" @[ 265 , 329 , 30 , 30 ]\n{\ncommands @[ 310 , 344 , 67 , 21 ]\n{\nX = \"1000\" ;\n}\ntransitions {\nS3 -> S0 when default @[ 248 , 278 , 50 , 21 ]\n;\nS3 -> S2 when A == \"000\" @[ 388 , 313 , 78 , 21 ]\n;\n}\n}\n}")) fsm_entity_1: pin names not known; wires that end beside it: clock_1_out, in_11, in_12, in_14, out_16

  // Other names for the same wires on the sheet: branch = in_8; muxM = in_4; rIN = in_2; srcA = in_5; wIR = in_1;
  //   wM = in_7; wR = in_6
endmodule
